# Fritzing sketch loopback.perf_board.4.1 (saved by Fritzing 0.9.3b)
perfboards: 1

parts:
  Teensy1 = Teensy 4.0  # not connected
  Teensy2 = Teensy 3.6 (Basic)
  R6 = Resistor [tolerance=±10% resistance=470 package=THT]
  J9 = male pin header, 1 pin [form="♂ (male)"]
  J11 = male pin header, 1 pin [form="♂ (male)"]  # not connected
  R9 = TRIMPOT [package=3362u-2]
  R10 = TRIMPOT [package=3362u-2]
  R11 = TRIMPOT [package=3362u-2]
  J8 = female pin header, 24 pins [form="♀ (female)"]
  R5 = Resistor [tolerance=±10% resistance=470 package=THT]
  J12 = female pin header, 24 pins [form="♀ (female)"]
  R14 = TRIMPOT [package=3362u-2]
  R15 = TRIMPOT [package=3362u-2]
  R16 = TRIMPOT [package=3362u-2]
  J7 = female pin header, 20 pins [form="♀ (female)"]
  J13 = female pin header, 20 pins [form="♀ (female)"]
  J14 = female pin header, 4 pins [form="♀ (female)"]
  J6 = female pin header, 2 pins [form="♀ (female)"]  # not connected
  J15 = male pin header, 2 pins [form="♂ (male)"]  # not connected
  J16 = male pin header, 2 pins [form="♂ (male)"]

nets:
  N1: Teensy2.GND, J12.pin1, J13.pin11
  N2: Teensy2.D0, J12.pin2
  N3: Teensy2.D1, R9.CCW, J12.pin3
  N4: Teensy2.D2, J12.pin4
  N5: Teensy2.D3, J12.pin5
  N6: Teensy2.D4, R10.CCW, J12.pin6
  N7: Teensy2.D5, J12.pin7
  N8: Teensy2.D6, J12.pin8
  N9: Teensy2.D7, R11.CCW, J12.pin9
  N10: Teensy2.D8, J12.pin10
  N11: Teensy2.D9, R6.Pin_1, J12.pin11
  N12: Teensy2.D10, J8.pin12, J12.pin12
  N13: Teensy2.D11, J8.pin13, J12.pin13
  N14: Teensy2.D12, J12.pin14
  N15: Teensy2.D13, J13.pin10
  N16: Teensy2.D14, J7.pin9, J13.pin9
  N17: Teensy2.D15, J13.pin8
  N18: Teensy2.D16, J13.pin7
  N19: Teensy2.D17, Teensy2.D18, R5.Pin_1, R14.CCW, R15.CCW, R16.CW, J13.pin5, J13.pin6
  N20: Teensy2.D19, Teensy2.D20, J13.pin3, J13.pin4
  N21: Teensy2.D21, J13.pin2
  N22: Teensy2.D22, J13.pin1
  N23: Teensy2.D23, J14.pin1
  N24: Teensy2.3V3, Teensy2.3V3_1, J12.pin15, J14.pin2
  N25: Teensy2.AGND, J14.pin3, J16.pin1
  N26: Teensy2.Vin, J14.pin4
  N27: Teensy2.D24, J12.pin16
  N28: Teensy2.D25, J8.pin17, J12.pin17
  N29: Teensy2.D26, J12.pin18
  N30: Teensy2.D27, J12.pin19
  N31: Teensy2.D28, J12.pin20
  N32: Teensy2.D29, J12.pin21
  N33: Teensy2.D30, J12.pin22
  N34: Teensy2.D31, J12.pin23
  N35: Teensy2.D32, J12.pin24
  N36: Teensy2.D33, J13.pin20
  N37: Teensy2.D34, J13.pin19
  N38: Teensy2.D35, J13.pin18
  N39: Teensy2.D36, J13.pin17
  N40: Teensy2.D37, R5.Pin_0, J7.pin16, J13.pin16
  N41: Teensy2.D38, J13.pin15
  N42: Teensy2.D39, J13.pin14
  N43: Teensy2.A21/DAC0, J13.pin13
  N44: Teensy2.A22/DAC1, J13.pin12
  N45: J9.pin1, J7.pin3

custom parts:
  Teensy 4.0: The Teensy is a complete USB-based microcontoller development system, in a very small footprint, capable of implementing many types of projects. All programming is done via the USB port. No special programmer is needed, only a standard micro-USB cable and a PC or Macintosh with a USB port.
  Teensy 3.6 (Basic): The Teensy is a complete USB-based microcontoller development system, in a very small footprint, capable of implementing many types of projects. All programming is done via the USB port. No special programmer is needed, only a standard micro-USB cable and a PC or Macintosh with a USB port.
