# Fritzing sketch loopback_board (saved by Fritzing 0.9.3b)
perfboards: 1

parts:
  Teensy1 = Teensy 4.0
  Teensy2 = Teensy 3.6 (Basic)  # not connected
  R6 = Resistor [tolerance=±10% resistance=470 package=THT]
  J9 = male pin header, 1 pin [form="♂ (male)"]
  J11 = male pin header, 1 pin [form="♂ (male)"]  # not connected
  R9 = TRIMPOT [package=3362u-2]
  R10 = TRIMPOT [package=3362u-2]
  R11 = TRIMPOT [package=3362u-2]
  J8 = female pin header, 24 pins [form="♀ (female)"]
  R5 = Resistor [tolerance=±10% resistance=470 package=THT]
  J12 = female pin header, 24 pins [form="♀ (female)"]
  R14 = TRIMPOT [package=3362u-2]  # not connected
  R15 = TRIMPOT [package=3362u-2]  # not connected
  R16 = TRIMPOT [package=3362u-2]  # not connected
  J7 = female pin header, 20 pins [form="♀ (female)"]
  J13 = female pin header, 20 pins [form="♀ (female)"]
  J14 = female pin header, 4 pins [form="♀ (female)"]
  J6 = female pin header, 2 pins [form="♀ (female)"]  # not connected
  J15 = male pin header, 2 pins [form="♂ (male)"]  # not connected
  J16 = male pin header, 2 pins [form="♂ (male)"]

nets:
  N1: Teensy1.pin_1, Teensy1.pin_32, J12.pin1, J14.pin3, J16.pin1
  N2: Teensy1.pin_2, J12.pin2
  N3: Teensy1.pin_3, R9.CCW, J12.pin3
  N4: Teensy1.pin_4, J12.pin4
  N5: Teensy1.pin_5, J12.pin5
  N6: Teensy1.pin_6, R10.CCW, J12.pin6
  N7: Teensy1.pin_7, J12.pin7
  N8: Teensy1.pin_8, J12.pin8
  N9: Teensy1.pin_9, R11.CCW, J12.pin9
  N10: Teensy1.pin_10, R6.Pin_1, J12.pin10
  N11: Teensy1.pin_11, J12.pin11
  N12: Teensy1.pin_12, J12.pin12
  N13: Teensy1.pin_13, J12.pin13
  N14: Teensy1.pin_14, J12.pin14
  N15: Teensy1.pin_20, J13.pin10
  N16: Teensy1.pin_21, R5.Pin_0, J13.pin9
  N17: Teensy1.pin_22, J13.pin8
  N18: Teensy1.pin_23, J13.pin7
  N19: Teensy1.pin_24, Teensy1.pin_25, J8.pin17, J13.pin5, J13.pin6
  N20: Teensy1.pin_26, J13.pin4
  N21: Teensy1.pin_27, J13.pin3
  N22: Teensy1.pin_28, J13.pin2
  N23: Teensy1.pin_29, J13.pin1
  N24: Teensy1.pin_30, J14.pin1
  N25: Teensy1.pin_31, J14.pin2
  N26: Teensy1.pin33, J14.pin4
  N27: J9.pin1, J8.pin16, J7.pin3

custom parts:
  Teensy 4.0: The Teensy is a complete USB-based microcontoller development system, in a very small footprint, capable of implementing many types of projects. All programming is done via the USB port. No special programmer is needed, only a standard micro-USB cable and a PC or Macintosh with a USB port.
  Teensy 3.6 (Basic): The Teensy is a complete USB-based microcontoller development system, in a very small footprint, capable of implementing many types of projects. All programming is done via the USB port. No special programmer is needed, only a standard micro-USB cable and a PC or Macintosh with a USB port.
